# Fritzing sketch 8-bit-computer (saved by Fritzing 0.9.6b)
breadboards: 14

parts:
  Breadboard2 = Breadboard Powerstrip
  Breadboard3 = Breadboard Powerstrip
  Breadboard4 = Breadboard Powerstrip
  Breadboard5 = Breadboard Powerstrip
  Breadboard6 = Breadboard Powerstrip
  Breadboard7 = Breadboard Powerstrip
  Breadboard8 = Breadboard Powerstrip
  Breadboard9 = Breadboard Powerstrip
  IC1 = IC, DIP package, 14 pins [chip_label=SN74LS08N]
  IC2 = IC, DIP package, 14 pins [chip_label=SN74LS04N]
  IC3 = IC, DIP package, 14 pins [chip_label=74LS32]
  IC4 = IC, DIP package, 8 pins [chip_label=LM555]
  IC5 = IC, DIP package, 8 pins [chip_label=NE555]
  IC6 = IC, DIP package, 8 pins [chip_label=LM555]
  S1 = Pushbutton [package="[THT]"]
  U2 = POT [package=3362u]
  S5 = Toggle Switch [package=THT]
  SW2 = DIP SWITCH [package=dipswitch-02]
  SW3 = DIP SWITCH [package=dipswitch-02]
  IC7 = IC, DIP package, 16 pins [chip_label=SN74LS173AN]
  IC8 = IC, DIP package, 16 pins [chip_label=SN74LS157N]
  IC9 = IC, DIP package, 16 pins [chip_label=SN74189N]
  IC10 = IC, DIP package, 16 pins [chip_label=SN74189N]
  IC11 = IC, DIP package, 14 pins [chip_label=SN74LS04N]
  IC12 = IC, DIP package, 14 pins [chip_label=SN74LS04N]
  IC13 = IC, DIP package, 20 pins [chip_label=SN74LS245N]
  S6 = Pushbutton [package="[THT]"]
  S7 = Toggle Switch [package=THT]
  SW4 = DIP Switch 8 Position [package=dipswitch-08]
  IC14 = IC, DIP package, 16 pins [chip_label=SN74LS157N]
  IC15 = IC, DIP package, 16 pins [chip_label=SN74LS157N]
  IC16 = IC, DIP package, 16 pins [chip_label=SN74LS157N]
  IC17 = IC, DIP package, 14 pins [chip_label=SN74LS00N]
  S8 = Pushbutton [package="[THT]"]
  IC18 = IC, DIP package, 14 pins [chip_label=SN74LS00N]
  IC19 = IC, DIP package, 20 pins [chip_label=SN74LS245N]
  IC20 = IC, DIP package, 16 pins [chip_label=74LS173N]
  IC21 = IC, DIP package, 16 pins [chip_label=74LS173N]
  IC22 = IC, DIP package, 16 pins [chip_label=SN74LS161N]
  IC23 = IC, DIP package, 16 pins [chip_label=SN74LS138N]
  IC24 = IC, DIP package, 24 pins [chip_label=CAT28C16AP]
  IC25 = IC, DIP package, 24 pins [chip_label=CAT28C16AP]
  IC26 = IC, DIP package, 20 pins [chip_label=SN74LS245N]
  IC27 = IC, DIP package, 16 pins [chip_label=SN74LS161N]
  IC28 = IC, DIP package, 20 pins [chip_label=SN74LS245N]
  IC29 = IC, DIP package, 20 pins [chip_label=SN74LS245N]
  IC30 = IC, DIP package, 20 pins [chip_label=SN74LS245N]
  IC31 = IC, DIP package, 16 pins [chip_label=74LS173N]
  IC32 = IC, DIP package, 16 pins [chip_label=74LS173N]
  IC33 = IC, DIP package, 16 pins [chip_label=SN74LS173AN]
  IC34 = IC, DIP package, 16 pins [chip_label=74LS173N]
  IC35 = IC, DIP package, 16 pins [chip_label=74LS173N]
  IC36 = IC, DIP package, 16 pins [chip_label=SN74LS283N]
  IC37 = IC, DIP package, 16 pins [chip_label=SN74LS283N]
  IC38 = IC, DIP package, 14 pins [chip_label=SN74LS86N]
  IC39 = IC, DIP package, 14 pins [chip_label=SN74LS86N]
  IC40 = IC, DIP package, 14 pins [chip_label=SN74LS08N]
  IC41 = IC, DIP package, 14 pins [chip_label=SN74LS02N]
  IC42 = IC, DIP package, 8 pins [chip_label=MC555]
  IC43 = IC, DIP package, 14 pins [chip_label=SN74LS107N]
  IC44 = IC, DIP package, 16 pins [chip_label=DM74LS139N]
  IC45 = IC, DIP package, 24 pins [chip_label=CAT28C16AP]
  DI1 = 7-Segment LED Display [package=THT]  # not connected
  DI2 = 7-Segment LED Display [package=THT]  # not connected
  DI3 = 7-Segment LED Display [package=THT]  # not connected
  DI4 = 7-Segment LED Display [package=THT]  # not connected
  IC46 = IC, DIP package, 20 pins [chip_label=SN74LS273N]
  IC47 = IC, DIP package, 14 pins [chip_label=SN74LS08N]
  IC48 = IC, DIP package, 14 pins [chip_label=SN74LS04N]
  IC49 = IC, DIP package, 14 pins [chip_label=SN74LS04N]
  R2 = Resistor Mini [tolerance=±5% resistance=220 package=THT]
  R4 = Resistor [tolerance=±5% power=0.25 resistance=220 package=THT]
  C1 = Ceramic Capacitor [capacitance=100nF voltage=35V package="100 mil [THT, multilayer]"]
  R5 = Resistor Mini [tolerance=±5% resistance=220 package=THT]
  R6 = Resistor Mini [tolerance=±5% resistance=220 package=THT]
  R7 = Resistor Mini [tolerance=±5% resistance=220 package=THT]
  R8 = Resistor Mini [tolerance=±5% resistance=220 package=THT]
  R9 = Resistor Mini [tolerance=±5% resistance=220 package=THT]
  R10 = Resistor Mini [tolerance=±5% resistance=220 package=THT]
  R11 = Resistor Mini [tolerance=±5% resistance=220 package=THT]
  R12 = Resistor Mini [tolerance=±5% resistance=220 package=THT]
  R13 = Resistor Mini [tolerance=±5% resistance=220 package=THT]
  R14 = Resistor Mini [tolerance=±5% resistance=220 package=THT]
  R15 = Resistor Mini [tolerance=±5% resistance=220 package=THT]
  R16 = Resistor Mini [tolerance=±5% resistance=220 package=THT]
  R18 = Resistor Mini [tolerance=±5% resistance=220 package=THT]
  R19 = Resistor Mini [tolerance=±5% resistance=220 package=THT]
  R20 = Resistor Mini [tolerance=±5% resistance=220 package=THT]
  C5 = Ceramic Capacitor [capacitance=100nF voltage=35V package="100 mil [THT, multilayer]"]
  C7 = Ceramic Capacitor [capacitance=100nF voltage=35V package="100 mil [THT, multilayer]"]
  C8 = Ceramic Capacitor [capacitance=100nF voltage=35V package="100 mil [THT, multilayer]"]
  LED4 = LED - 3mm [color="Yellow (585nm)" current=0.030 package="3 mm [THT]"]
  LED3 = LED - 3mm [color="Yellow (585nm)" current=0.030 package="3 mm [THT]"]
  LED46 = LED - 3mm [color="Green (555nm)" current=0.030 package="3 mm [THT]"]
  LED47 = LED - 3mm [color="Green (555nm)" current=0.030 package="3 mm [THT]"]
  LED48 = LED - 3mm [color="Green (555nm)" current=0.030 package="3 mm [THT]"]
  LED49 = LED - 3mm [color="Green (555nm)" current=0.030 package="3 mm [THT]"]
  LED36 = LED - 3mm [color="Red (633nm)" current=0.030 package="3 mm [THT]"]
  LED37 = LED - 3mm [color="Red (633nm)" current=0.030 package="3 mm [THT]"]
  LED38 = LED - 3mm [color="Red (633nm)" current=0.030 package="3 mm [THT]"]
  LED39 = LED - 3mm [color="Red (633nm)" current=0.030 package="3 mm [THT]"]
  LED40 = LED - 3mm [color="Red (633nm)" current=0.030 package="3 mm [THT]"]
  LED41 = LED - 3mm [color="Red (633nm)" current=0.030 package="3 mm [THT]"]
  LED42 = LED - 3mm [color="Red (633nm)" current=0.030 package="3 mm [THT]"]
  LED43 = LED - 3mm [color="Red (633nm)" current=0.030 package="3 mm [THT]"]
  LED103 = LED Red 3mm - Top [color="Yellow (585nm)" package="3 mm [THT] Top"]
  LED104 = LED Red 3mm - Top [color="Yellow (585nm)" package="3 mm [THT] Top"]
  LED105 = LED Red 3mm - Top [color="Yellow (585nm)" package="3 mm [THT] Top"]
  LED106 = LED Red 3mm - Top [color="Yellow (585nm)" package="3 mm [THT] Top"]
  LED107 = LED Red 3mm - Top [color="Green (555nm)" package="3 mm [THT] Top"]
  LED108 = LED Red 3mm - Top [color="Red (633nm)" package="3 mm [THT] Top"]
  C9 = Tantalum Capacitor top [capacitance=1µF voltage=35V package="100 mil [THT, Tantalum]"]
  R21 = Vertical Resistor [tolerance=±5% resistance=220 package=THT]
  R22 = Vertical Resistor [tolerance=±5% resistance=220 package=THT]
  LED110 = LED Red 3mm - Top [color="Blue (505nm)" package="3 mm [THT] Top"]
  R23 = Vertical Resistor [tolerance=±5% resistance=220 package=THT]
  LED111 = LED Red 3mm - Top [color="Blue (505nm)" package="3 mm [THT] Top"]
  R24 = Vertical Resistor [tolerance=±5% resistance=220 package=THT]
  R25 = Vertical Resistor [tolerance=±5% resistance=220 package=THT]
  R26 = Vertical Resistor [tolerance=±5% resistance=220 package=THT]
  R27 = Vertical Resistor [tolerance=±5% resistance=220 package=THT]
  LED112 = LED Red 3mm - Top [color="Blue (505nm)" package="3 mm [THT] Top"]
  LED113 = LED Red 3mm - Top [color="Blue (505nm)" package="3 mm [THT] Top"]
  LED114 = LED Red 3mm - Top [color="Blue (505nm)" package="3 mm [THT] Top"]
  LED115 = LED Red 3mm - Top [color="Blue (505nm)" package="3 mm [THT] Top"]
  LED116 = LED Red 3mm - Top [color="Blue (505nm)" package="3 mm [THT] Top"]
  LED117 = LED Red 3mm - Top [color="Blue (505nm)" package="3 mm [THT] Top"]
  LED118 = LED Red 3mm - Top [color="Blue (505nm)" package="3 mm [THT] Top"]
  LED119 = LED Red 3mm - Top [color="Blue (505nm)" package="3 mm [THT] Top"]
  R28 = Vertical Resistor [tolerance=±5% resistance=220 package=THT]
  R29 = Vertical Resistor [tolerance=±5% resistance=220 package=THT]
  R30 = Vertical Resistor [tolerance=±5% resistance=220 package=THT]
  R31 = Vertical Resistor [tolerance=±5% resistance=220 package=THT]
  R32 = Vertical Resistor [tolerance=±5% resistance=220 package=THT]
  LED120 = LED Red 3mm - Top [color="Blue (505nm)" package="3 mm [THT] Top"]
  LED121 = LED Red 3mm - Top [color="Blue (505nm)" package="3 mm [THT] Top"]
  LED122 = LED Red 3mm - Top [color="Blue (505nm)" package="3 mm [THT] Top"]
  LED123 = LED Red 3mm - Top [color="Blue (505nm)" package="3 mm [THT] Top"]
  LED124 = LED Red 3mm - Top [color="Blue (505nm)" package="3 mm [THT] Top"]
  R33 = Vertical Resistor [tolerance=±5% resistance=220 package=THT]
  R34 = Vertical Resistor [tolerance=±5% resistance=220 package=THT]
  R35 = Vertical Resistor [tolerance=±5% resistance=220 package=THT]
  R36 = Vertical Resistor [tolerance=±5% resistance=220 package=THT]
  R37 = Vertical Resistor [tolerance=±5% resistance=220 package=THT]
  R38 = Vertical Resistor [tolerance=±5% resistance=220 package=THT]
  LED125 = LED Red 3mm - Top [color="Blue (505nm)" package="3 mm [THT] Top"]
  LED126 = LED Red 3mm - Top [color="Blue (505nm)" package="3 mm [THT] Top"]
  LED127 = LED Red 3mm - Top [color="Blue (505nm)" package="3 mm [THT] Top"]
  R39 = Vertical Resistor [tolerance=±5% resistance=220 package=THT]
  R40 = Vertical Resistor [tolerance=±5% resistance=220 package=THT]
  LED129 = LED Red 3mm - Top [color="Red (633nm)" package="3 mm [THT] Top"]
  LED131 = LED Red 3mm - Top [color="Red (633nm)" package="3 mm [THT] Top"]
  LED132 = LED Red 3mm - Top [color="Red (633nm)" package="3 mm [THT] Top"]
  LED133 = LED Red 3mm - Top [color="Red (633nm)" package="3 mm [THT] Top"]
  LED96 = LED - 3mm [color="Yellow (585nm)" current=0.030 package="3 mm [THT]"]
  C10 = Tantalum Capacitor top [capacitance=1µF voltage=35V package="100 mil [THT, Tantalum]"]
  C4 = Ceramic Capacitor [capacitance=100nF voltage=35V package="100 mil [THT, multilayer]"]
  C11 = Tantalum Capacitor top [capacitance=1µF voltage=35V package="100 mil [THT, Tantalum]"]
  LED134 = LED Red 3mm - Top [color="Red (633nm)" package="3 mm [THT] Top"]
  LED135 = LED Red 3mm - Top [color="Red (633nm)" package="3 mm [THT] Top"]
  LED136 = LED Red 3mm - Top [color="Red (633nm)" package="3 mm [THT] Top"]
  LED137 = LED Red 3mm - Top [color="Red (633nm)" package="3 mm [THT] Top"]
  LED138 = LED - 3mm [color="Blue (505nm)" current=0.030 package="3 mm [THT]"]
  LED139 = LED Red 3mm - Top [color="Blue (505nm)" package="3 mm [THT] Top"]
  C12 = Tantalum Capacitor top [capacitance=1µF voltage=35V package="100 mil [THT, Tantalum]"]
  LED140 = LED Red 3mm - Top [color="Red (633nm)" package="3 mm [THT] Top"]
  C13 = Tantalum Capacitor top [capacitance=1µF voltage=35V package="100 mil [THT, Tantalum]"]
  R41 = Vertical Resistor [tolerance=±5% resistance=220 package=THT]
  LED141 = LED Red 3mm - Top [color="Red (633nm)" package="3 mm [THT] Top"]
  LED142 = LED Red 3mm - Top [color="Red (633nm)" package="3 mm [THT] Top"]
  LED143 = LED Red 3mm - Top [color="Green (555nm)" package="3 mm [THT] Top"]
  LED144 = LED Red 3mm - Top [color="Green (555nm)" package="3 mm [THT] Top"]
  LED145 = LED Red 3mm - Top [color="Green (555nm)" package="3 mm [THT] Top"]
  LED146 = LED Red 3mm - Top [color="Green (555nm)" package="3 mm [THT] Top"]
  LED147 = LED Red 3mm - Top [color="Green (555nm)" package="3 mm [THT] Top"]
  LED148 = LED Red 3mm - Top [color="Red (633nm)" package="3 mm [THT] Top"]
  LED149 = LED Red 3mm - Top [color="Red (633nm)" package="3 mm [THT] Top"]
  LED150 = LED Red 3mm - Top [color="Red (633nm)" package="3 mm [THT] Top"]
  LED151 = LED Red 3mm - Top [color="Red (633nm)" package="3 mm [THT] Top"]
  LED152 = LED Red 3mm - Top [color="Red (633nm)" package="3 mm [THT] Top"]
  LED153 = LED Red 3mm - Top [color="Red (633nm)" package="3 mm [THT] Top"]
  LED154 = LED Red 3mm - Top [color="Red (633nm)" package="3 mm [THT] Top"]
  LED155 = LED Red 3mm - Top [color="Red (633nm)" package="3 mm [THT] Top"]
  LED156 = LED Red 3mm - Top [color="Red (633nm)" package="3 mm [THT] Top"]
  LED157 = LED Red 3mm - Top [color="Red (633nm)" package="3 mm [THT] Top"]
  LED158 = LED Red 3mm - Top [color="Red (633nm)" package="3 mm [THT] Top"]
  LED159 = LED Red 3mm - Top [color="Red (633nm)" package="3 mm [THT] Top"]
  LED160 = LED Red 3mm - Top [color="Red (633nm)" package="3 mm [THT] Top"]
  LED161 = LED Red 3mm - Top [color="Red (633nm)" package="3 mm [THT] Top"]
  LED162 = LED Red 3mm - Top [color="Red (633nm)" package="3 mm [THT] Top"]
  LED163 = LED Red 3mm - Top [color="Red (633nm)" package="3 mm [THT] Top"]
  LED164 = LED Red 3mm - Top [color="Green (555nm)" package="3 mm [THT] Top"]
  LED165 = LED Red 3mm - Top [color="Green (555nm)" package="3 mm [THT] Top"]
  LED166 = LED Red 3mm - Top [color="Blue (470nm)" package="3 mm [THT] Top"]
  LED167 = LED Red 3mm - Top [color="Blue (470nm)" package="3 mm [THT] Top"]
  LED168 = LED Red 3mm - Top [color="Red (633nm)" package="3 mm [THT] Top"]
  LED169 = LED Red 3mm - Top [color="Red (633nm)" package="3 mm [THT] Top"]
  LED170 = LED Red 3mm - Top [color="Red (633nm)" package="3 mm [THT] Top"]
  LED171 = LED Red 3mm - Top [color="Red (633nm)" package="3 mm [THT] Top"]
  LED172 = LED Red 3mm - Top [color="Red (633nm)" package="3 mm [THT] Top"]
  LED173 = LED Red 3mm - Top [color="Red (633nm)" package="3 mm [THT] Top"]
  LED174 = LED Red 3mm - Top [color="Red (633nm)" package="3 mm [THT] Top"]
  LED175 = LED Red 3mm - Top [color="Red (633nm)" package="3 mm [THT] Top"]
  LED176 = LED Red 3mm - Top [color="Blue (505nm)" package="3 mm [THT] Top"]
  LED177 = LED Red 3mm - Top [color="Yellow (585nm)" package="3 mm [THT] Top"]
  LED178 = LED Red 3mm - Top [color="Blue (505nm)" package="3 mm [THT] Top"]
  LED179 = LED Red 3mm - Top [color="Yellow (585nm)" package="3 mm [THT] Top"]
  LED180 = LED Red 3mm - Top [color="Blue (505nm)" package="3 mm [THT] Top"]
  LED181 = LED Red 3mm - Top [color="Yellow (585nm)" package="3 mm [THT] Top"]
  LED182 = LED Red 3mm - Top [color="Blue (505nm)" package="3 mm [THT] Top"]
  LED183 = LED Red 3mm - Top [color="Yellow (585nm)" package="3 mm [THT] Top"]
  C14 = Tantalum Capacitor top [capacitance=1µF voltage=35V package="100 mil [THT, Tantalum]"]
  C15 = Tantalum Capacitor top [capacitance=1µF voltage=35V package="100 mil [THT, Tantalum]"]
  C16 = Tantalum Capacitor top [capacitance=1µF voltage=35V package="100 mil [THT, Tantalum]"]
  C17 = Tantalum Capacitor top [capacitance=1µF voltage=35V package="100 mil [THT, Tantalum]"]
  C18 = Tantalum Capacitor top [capacitance=1µF voltage=35V package="100 mil [THT, Tantalum]"]
  C19 = Tantalum Capacitor top [capacitance=1µF voltage=35V package="100 mil [THT, Tantalum]"]
  C20 = Tantalum Capacitor top [capacitance=1µF voltage=35V package="100 mil [THT, Tantalum]"]
  C21 = Tantalum Capacitor top [capacitance=1µF voltage=35V package="100 mil [THT, Tantalum]"]
  R42 = Vertical Resistor [tolerance=±5% resistance=220 package=THT]
  C26 = Electrolytic Capacitor [capacitance=100µF voltage=35V package="200 mil [THT, electrolytic]"]
  C27 = Electrolytic Capacitor [capacitance=100µF voltage=35V package="200 mil [THT, electrolytic]"]
  R43 = Vertical Resistor [tolerance=±5% resistance=220 package=THT]
  C28 = Ceramic Capacitor [capacitance="100 nF" voltage=35V package="0805 [SMD, multilayer]"]
  C29 = Ceramic Capacitor [capacitance="100 nF" voltage=35V package="0805 [SMD, multilayer]"]
  C30 = Tantalum Capacitor top [capacitance=1µF voltage=35V package="100 mil [THT, Tantalum]"]
  C31 = Tantalum Capacitor top [capacitance=1µF voltage=35V package="100 mil [THT, Tantalum]"]
  C32 = Tantalum Capacitor top [capacitance=1µF voltage=35V package="100 mil [THT, Tantalum]"]
  C33 = Ceramic Capacitor [capacitance=100nF voltage=35V package="100 mil [THT, multilayer]"]
  R44 = Vertical Resistor [tolerance=±5% resistance=220 package=THT]
  C34 = Ceramic Capacitor [capacitance="100 nF" voltage=35V package="0805 [SMD, multilayer]"]
  C35 = Ceramic Capacitor [capacitance=100nF voltage=35V package="100 mil [THT, multilayer]"]
  C36 = Ceramic Capacitor [capacitance=100nF voltage=35V package="100 mil [THT, multilayer]"]

nets:
  N1: Breadboard2.pin3Y, Breadboard2.pin6Y, Breadboard2.pin61Y, Breadboard8.pin3Y, R12.Pin_1, LED38.anode
  N2: Breadboard2.pin3Z, Breadboard2.pin7Z, Breadboard2.pin61Z, Breadboard8.pin3Z, R13.Pin_1, LED39.anode
  N3: Breadboard3.pin3Y, Breadboard3.pin7Y, Breadboard3.pin61Y, Breadboard7.pin3Y, R16.Pin_0, LED40.anode
  N4: Breadboard3.pin3Z, Breadboard3.pin6Z, Breadboard3.pin61Z, Breadboard7.pin3Z, R15.Pin_0, LED41.anode
  N5: Breadboard4.pin3Y, Breadboard4.pin6Y, Breadboard4.pin61Y, Breadboard6.pin3Y, R14.Pin_0, LED42.anode
  N6: Breadboard4.pin3Z, Breadboard4.pin5Z, Breadboard4.pin61Z, Breadboard6.pin3Z, R10.Pin_0, LED43.anode
  N7: Breadboard5.pin3Y, Breadboard5.pin5Y, Breadboard5.pin61Y, Breadboard9.pin3Y, R9.Pin_1, LED36.anode
  N8: Breadboard5.pin3Z, Breadboard5.pin6Z, Breadboard5.pin61Z, Breadboard9.pin3Z, R11.Pin_1, LED37.anode
  N9: IC1.pin7, IC2.pin7, IC3.pin7, IC4.pin1, IC5.pin1, IC6.pin1, S1.Pin_3, S1.Pin_4, S5.COM, SW2.1, SW2.2, SW3.3, SW3.4, IC7.pin8, IC9.pin8, IC10.pin8, IC11.pin7, IC12.pin7, IC13.pin10, S7.COM, SW4.3, SW4.4, SW4.7, SW4.8, SW4.11, SW4.12, SW4.15, IC14.pin8, IC15.pin8, IC16.pin8, IC17.pin7, IC18.pin7, IC19.pin10, IC20.pin8, IC21.pin8, IC22.pin8, IC23.pin8, IC24.pin12, IC25.pin12, IC26.pin10, IC27.pin8, IC28.pin10, IC29.pin10, IC30.pin10, IC31.pin8, IC32.pin8, IC33.pin8, IC34.pin8, IC35.pin8, IC36.pin8, IC37.pin8, IC38.pin7, IC39.pin7, IC40.pin7, IC41.pin7, IC42.pin1, IC43.pin7, IC44.pin8, IC45.pin12, IC46.pin10, IC47.pin7, IC48.pin7, IC49.pin7, C1.0, R5.Pin_1, R6.Pin_1, R7.Pin_1, R9.Pin_0, R10.Pin_1, R11.Pin_0, R12.Pin_0, R13.Pin_0, R14.Pin_1, R16.Pin_1, C5.0, C7.0, C8.0, LED46.cathode, LED47.cathode, LED48.cathode, LED49.cathode, LED36.cathode, LED37.cathode, LED38.cathode, LED39.cathode, LED40.cathode, LED41.cathode, LED42.cathode, LED43.cathode, LED103.cathode, LED104.cathode, LED105.cathode, LED106.cathode, C9.-, R21.Pin_0, R22.Pin_0, R23.Pin_1, R24.Pin_1, R25.Pin_1, R26.Pin_1, R27.Pin_1, R28.Pin_1, R29.Pin_1, R30.Pin_1, R31.Pin_1, R32.Pin_1, R33.Pin_1, R34.Pin_1, R35.Pin_1, R36.Pin_1, R37.Pin_1, R38.Pin_1, R39.Pin_1, R40.Pin_1, LED129.cathode, LED131.cathode, LED132.cathode, LED133.cathode, C10.-, C4.1, C11.-, LED134.cathode, LED135.cathode, LED136.cathode, LED137.cathode, C12.-, LED140.cathode, C13.-, R41.Pin_0, LED141.cathode, LED142.cathode, LED143.cathode, LED144.cathode, LED145.cathode, LED146.cathode, LED147.cathode, LED148.cathode, LED149.cathode, LED150.cathode, LED151.cathode, LED152.cathode, LED153.cathode, LED154.cathode, LED155.cathode, LED156.cathode, LED157.cathode, LED158.cathode, LED159.cathode, LED160.cathode, LED161.cathode, LED162.cathode, LED163.cathode, LED164.anode, LED165.anode, LED166.cathode, LED167.cathode, LED168.cathode, LED169.cathode, LED170.cathode, LED171.cathode, LED172.cathode, LED173.cathode, LED174.cathode, LED175.cathode, LED176.cathode, LED177.cathode, LED178.cathode, LED179.cathode, LED180.cathode, LED181.cathode, LED182.cathode, LED183.cathode, C14.-, C15.-, C16.-, C17.-, C18.-, C19.-, C20.-, C21.-, C26.-, C27.-, C28.0, C29.0, C30.-, C31.-, R44.Pin_1, C35.0, C36.1
  N10: IC1.pin8, LED138.anode
  N11: IC1.pin14, IC2.pin14, IC3.pin14, IC4.pin8, IC5.pin8, IC6.pin8, IC7.pin16, IC8.pin16, IC9.pin16, IC10.pin16, IC11.pin14, IC12.pin14, IC13.pin20, IC14.pin16, IC15.pin16, IC16.pin16, IC17.pin14, S8.Pin_3, S8.Pin_4, IC18.pin14, IC19.pin20, IC20.pin16, IC21.pin16, IC22.pin16, IC23.pin16, IC24.pin24, IC25.pin24, IC26.pin20, IC27.pin16, IC28.pin20, IC29.pin20, IC30.pin20, IC31.pin16, IC32.pin16, IC33.pin16, IC34.pin16, IC35.pin16, IC36.pin16, IC37.pin16, IC38.pin14, IC39.pin14, IC40.pin14, IC41.pin14, IC42.pin8, IC43.pin14, IC44.pin16, IC45.pin24, IC46.pin20, IC47.pin14, IC48.pin14, IC49.pin14, R2.Pin_0, R8.Pin_0, R18.Pin_1, R19.Pin_1, R20.Pin_1, LED107.anode, LED108.anode, C9.+, C10.+, C11.+, C12.+, C13.+, C14.+, C15.+, C16.+, C18.+, C19.+, C20.+, C21.+, C26.+, C27.+, R43.Pin_1, C30.+, C31.+, C32.+, C33.0, C36.0
  N12: IC4.pin2, C4.0
  N13: IC4.pin3, LED96.anode
  N14: IC4.pin5, C1.1
  N15: IC4.pin7, R2.Pin_1, R4.Pin_1
  N16: IC5.pin3, LED3.anode
  N17: IC5.pin5, C8.1
  N18: IC5.pin6, C7.1
  N19: IC5.pin7, R8.Pin_1
  N20: IC6.pin2, R18.Pin_0
  N21: IC6.pin3, LED4.anode
  N22: IC6.pin4, R19.Pin_0
  N23: IC6.pin5, C5.1
  N24: S1.Pin_1, S1.Pin_2, R20.Pin_0
  N25: U2.E, R4.Pin_0
  N26: IC11.pin2, LED154.anode
  N27: IC11.pin4, LED148.anode
  N28: IC11.pin6, LED150.anode
  N29: IC12.pin2, LED155.anode
  N30: IC12.pin4, LED149.anode
  N31: IC12.pin6, LED151.anode
  N32: S6.Pin_1, S6.Pin_2
  N33: S6.Pin_3, S6.Pin_4
  N34: IC14.pin12, C33.1
  N35: IC17.pin1, R44.Pin_0, C34.1
  N36: S8.Pin_1, S8.Pin_2, R41.Pin_1
  N37: IC20.pin3, LED181.anode
  N38: IC20.pin4, LED183.anode
  N39: IC20.pin5, LED177.anode
  N40: IC20.pin6, LED179.anode
  N41: IC21.pin3, LED182.anode
  N42: IC21.pin4, LED176.anode
  N43: IC21.pin5, LED178.anode
  N44: IC21.pin6, LED180.anode
  N45: IC22.pin2, LED139.anode
  N46: IC22.pin13, LED142.anode
  N47: IC22.pin14, LED141.anode
  N48: IC22.pin15, LED140.anode
  N49: IC23.pin11, LED147.anode
  N50: IC23.pin12, LED146.anode
  N51: IC23.pin13, LED145.anode
  N52: IC23.pin14, LED144.anode
  N53: IC23.pin15, LED143.anode
  N54: IC26.pin11, LED49.anode
  N55: IC26.pin12, LED48.anode
  N56: IC26.pin13, LED47.anode
  N57: IC26.pin14, LED46.anode
  N58: IC29.pin2, LED174.anode
  N59: IC29.pin3, LED168.anode
  N60: IC29.pin4, LED170.anode
  N61: IC29.pin5, LED172.anode
  N62: IC29.pin6, LED173.anode
  N63: IC29.pin7, LED175.anode
  N64: IC29.pin8, LED169.anode
  N65: IC29.pin9, LED171.anode
  N66: IC31.pin3, LED162.anode
  N67: IC31.pin4, LED156.anode
  N68: IC31.pin5, LED158.anode
  N69: IC31.pin6, LED160.anode
  N70: IC32.pin3, LED161.anode
  N71: IC32.pin4, LED163.anode
  N72: IC32.pin5, LED157.anode
  N73: IC32.pin6, LED159.anode
  N74: IC33.pin3, LED165.cathode
  N75: IC33.pin4, LED164.cathode
  N76: IC33.pin15, C35.1
  N77: IC34.pin3, LED137.anode
  N78: IC34.pin4, LED134.anode
  N79: IC34.pin5, LED135.anode
  N80: IC34.pin6, LED136.anode
  N81: IC35.pin3, LED133.anode
  N82: IC35.pin4, LED129.anode
  N83: IC35.pin5, LED131.anode
  N84: IC35.pin6, LED132.anode
  N85: IC36.pin9, LED166.anode
  N86: IC40.pin8, LED167.anode
  N87: IC42.pin2, C29.1
  N88: IC42.pin5, C28.1
  N89: IC42.pin6, R42.Pin_1
  N90: IC42.pin7, R42.Pin_0, R43.Pin_0
  N91: R5.Pin_0, LED96.cathode
  N92: R6.Pin_0, LED3.cathode
  N93: R7.Pin_0, LED4.cathode
  N94: R21.Pin_1, LED139.cathode
  N95: R22.Pin_1, LED138.cathode
  N96: LED110.cathode, R23.Pin_0
  N97: LED111.cathode, R24.Pin_0
  N98: R25.Pin_0, LED112.cathode
  N99: R26.Pin_0, LED113.cathode
  N100: R27.Pin_0, LED114.cathode
  N101: LED115.cathode, R28.Pin_0
  N102: LED116.cathode, R29.Pin_0
  N103: LED117.cathode, R30.Pin_0
  N104: LED118.cathode, R31.Pin_0
  N105: LED119.cathode, R32.Pin_0
  N106: LED120.cathode, R33.Pin_0
  N107: LED121.cathode, R34.Pin_0
  N108: LED122.cathode, R35.Pin_0
  N109: LED123.cathode, R36.Pin_0
  N110: LED124.cathode, R37.Pin_0
  N111: R38.Pin_0, LED125.cathode
  N112: LED126.cathode, R39.Pin_0
  N113: LED127.cathode, R40.Pin_0

notes:
  Clock
  Memory Address Register
  Instruction Decoder
  Instruction Register
  Step Counter
  Random Access Memory
  Bus
  Program Counter
  A Register
  B Register
  Arithmetic Logic Unit
  Flags Register
  Reset Button
  Program Button
  Single Step Button
  Run/Program Mode Switch
  Auto/Single Step Mode Switch
  Frequency Potentiometer
  Control Word
  Output Register
  HLT MI RI RO II IO AI AO BI BO S- SO OI O- CE CO CJ FI
  CF ZF
  Z
  C
  Programmer

custom parts:
  Breadboard Powerstrip: A breadboard for easily prototyping circuits
  Resistor Mini: A generic resistor (0.25W)
  LED Red 3mm - Top: A generic red LED (~1.8V)
  Tantalum Capacitor top: Top view Tantalum capacitor.
  Vertical Resistor: A generic resistor (0.25W)
  Vertical Resistor: A generic resistor (0.25W)
